# Fritzing sketch Sketsa rangkaian water level sensor (saved by Fritzing 0.9.3b)

parts:
  Part3 = Arduino Uno (Rev3) - ICSP
  Part6 = Arduino Prototyping Shield
  Water_Level_Sensor1 = Water Level Sensor
  T1 = LM34 Temperature Sensor [package="TO92 [THT]"]
  SP1 = SPEAKER [package=pcb_mount_speaker]
  S1 = Pushbutton [package="[THT]"]

nets:
  N1: Part3.A0, Part6.A0, Water_Level_Sensor1.SIG
  N2: Part3.D11_PWM/MOSI, Part6.D11, Part6.N$231
  GND: Part3.GND, Part6.GND, Part6.D7, Part6.N$232, Water_Level_Sensor1.GND, S1.Pin_3, S1.Pin_4
  5V: Part3.5V, Part6.+5V, Part6.N$360
  N3: Part6.N$155, SP1.+
  N4: Part6.N$167, T1.+Vs
  N5: Part6.N$229, T1.Vout
  N6: Part6.N$230, T1.GND
  N7: Part6.N$283, SP1.-
  N8: Part6.N$292, Water_Level_Sensor1.VCC

custom parts:
  Water Level Sensor: A water level sensor. This sensor operates at 3V to 5V. The Sig (signal) pin outputs an analogue signal that is in proportion to the amount of water in contact with the sensor.
