# Fritzing sketch Water Level Sensor (saved by Fritzing 0.9.3b)

parts:
  Part1 = Arduino Uno (Rev3) - ICSP
  Water_Level_Sensor1 = Water Level Sensor
  AMP2 = PAM8403 6W Stereo Amplifier
  SP1 = SPEAKER [package=pcb_mount_speaker]
  S2 = Pushbutton [package="[SMD]"]

nets:
  N1: Part1.D9_PWM, AMP2.INPUTL
  GND: Part1.GND, Part1.D7, Water_Level_Sensor1.GND, AMP2.POWER-, S2.Pin_3, S2.Pin_4
  N2: Part1.D2, Water_Level_Sensor1.SIG
  N3: Water_Level_Sensor1.VCC, AMP2.POWER+
  N4: AMP2.LOUT+, AMP2.LOUT-, SP1.+, SP1.-

custom parts:
  Water Level Sensor: A water level sensor. This sensor operates at 3V to 5V. The Sig (signal) pin outputs an analogue signal that is in proportion to the amount of water in contact with the sensor.
  PAM8403 6W Stereo Amplifier: PAM8403 6 Watt Stereo Amplifier
